// Digital circuit CPU.dig as structural Verilog
module CPU (
  input  [15:0] DATA_in,
  input  CLK,
  input  START,
  output [15:0] Data_out,
  output [5:0] Adress,
  output ME,
  output R_W
);

  wire unidad_de_control_1_p8, unidad_de_control_1_p9, unidad_de_control_1_p10, unidad_de_control_1_p11,
       unidad_de_control_1_p12, unidad_de_control_1_p13, unidad_de_ejecucion_1_c, unidad_de_ejecucion_1_n,
       unidad_de_ejecucion_1_z;

  Unidad_de_ejecucion unidad_de_ejecucion_1 (
    .EN_R0(unidad_de_control_1_p8), .EN_R1(unidad_de_control_1_p9), .LOAD_PC(unidad_de_control_1_p10),
    .STORE(unidad_de_control_1_p11), .ADRESS_PC____ADRESS_INSTRUCCION(unidad_de_control_1_p12),
    .CE_PC(unidad_de_control_1_p13), .DATA(DATA_in), .CLK(CLK), .Z(unidad_de_ejecucion_1_z),
    .N(unidad_de_ejecucion_1_n), .C(unidad_de_ejecucion_1_c), .DATA_SALIDA(Data_out), .ADRESS(Adress));
  // Unidad_de_control unidad_de_control_1: pin names not known; wires that end beside it: unidad_de_ejecucion_1_z, unidad_de_ejecucion_1_n, unidad_de_ejecucion_1_c, DATA_in, CLK, START, DATA_in, unidad_de_control_1_p8, unidad_de_control_1_p9, unidad_de_control_1_p10, unidad_de_control_1_p11, unidad_de_control_1_p12, unidad_de_control_1_p13, R_W, ME
endmodule
