// Digital circuit Unidad de control.dig as structural Verilog
module Unidad_de_control (
  input  Z,
  input  N,
  input  C,
  input  DATA,
  input  CLK,
  input  START,
  output EN_R0,
  output EN_R1,
  output LOAD_PC,
  output STORE,
  output ADRESS_PC____ADRESS_INSTRUCCION,
  output CE_PC,
  output R_W,
  output ME
);

  wire d_ff_2_q;

  or or_1 (ME, START, d_ff_2_q);
  assign ADRESS_PC____ADRESS_INSTRUCCION = ME ? ME : 1'bz;  // Driver driver_1
  D_FF d_ff_1 (.D(ME), .C(CLK), .Q(CE_PC));  // open: nQ
  assign ADRESS_PC____ADRESS_INSTRUCCION = CE_PC ? CE_PC : 1'bz;  // Driver driver_2
  D_FF d_ff_2 (.D(CE_PC), .C(CLK), .Q(d_ff_2_q));  // open: nQ

  assign EN_R0 = 1'b0;
  assign EN_R1 = 1'b0;
  assign LOAD_PC = 1'b0;
  assign R_W = ME;
  assign STORE = 1'b0;
endmodule
