// Digital circuit ALU.dig as structural Verilog
module ALU (
  input  [15:0] R0,
  input  [15:0] R1,
  input  [2:0] OP,
  output [15:0] result,
  output carry,
  output negative,
  output zero
);

  wire c_0, c_1, n_0, n_1, n_2, n_3, n_4, z_0, z_1, z_2, z_3, z_4, z_5, z_6;
  wire [15:0] not_1_out;
  wire [15:1] result_0, result_1, result_2, result_3, result_4;

  nand nand_1 (z_0, n_0, result_0[1], result_0[2], result_0[3], result_0[4], result_0[5], result_0[6], result_0[7], result_0[8], result_0[9], result_0[10], result_0[11], result_0[12], result_0[13], result_0[14], result_0[15]);
  Add #(.Bits(16)) add_1 (.a(R1), .b(R0), .c_i(1'b0), .s({result_0, n_0}), .c_o(c_0));
  nand nand_2 (z_1, n_1, result_1[1], result_1[2], result_1[3], result_1[4], result_1[5], result_1[6], result_1[7], result_1[8], result_1[9], result_1[10], result_1[11], result_1[12], result_1[13], result_1[14], result_1[15]);
  assign not_1_out = ~R1;  // Not not_1, 16 bits wide
  Add #(.Bits(16)) add_2 (.a(R0), .b(not_1_out), .c_i(1'b1), .s({result_1, n_1}), .c_o(c_1));
  nand nand_3 (z_2, n_2, result_2[1], result_2[2], result_2[3], result_2[4], result_2[5], result_2[6], result_2[7], result_2[8], result_2[9], result_2[10], result_2[11], result_2[12], result_2[13], result_2[14], result_2[15]);
  assign {result_2, n_2} = R0 & R1;  // And and_1, 16 bits wide
  nand nand_4 (z_3, n_3, result_3[1], result_3[2], result_3[3], result_3[4], result_3[5], result_3[6], result_3[7], result_3[8], result_3[9], result_3[10], result_3[11], result_3[12], result_3[13], result_3[14], result_3[15]);
  assign {result_3, n_3} = R1 | R0;  // Or or_1, 16 bits wide
  nand nand_5 (z_4, n_4, result_4[1], result_4[2], result_4[3], result_4[4], result_4[5], result_4[6], result_4[7], result_4[8], result_4[9], result_4[10], result_4[11], result_4[12], result_4[13], result_4[14], result_4[15]);
  assign {result_4, n_4} = ~R0;  // Not not_2, 16 bits wide
  nand nand_6 (z_5, 1'b0, R0[0], R0[1], R0[2], R0[3], R0[4], R0[5], R0[6], R0[7], R0[8], R0[9], R0[10], R0[11], R0[12], R0[13], R0[14]);
  nand nand_7 (z_6, R0[1], R0[2], R0[3], R0[4], R0[5], R0[6], R0[7], R0[8], R0[9], R0[10], R0[11], R0[12], R0[13], R0[14], R0[15], 1'b0);
  Multiplexer #(.Selector_Bits(3), .Bits(16)) multiplexer_1 (
    .sel(OP), .in_0({result_0, n_0}), .in_1({result_1, n_1}), .in_2({result_2, n_2}), .in_3({result_3, n_3}),
    .in_4({result_4, n_4}), .in_5({R0[14:0], 1'b0}), .in_6({1'b0, R0[15:1]}), .in_7({16{1'b1}}), .out(result));
  Multiplexer #(.Selector_Bits(3)) multiplexer_2 (
    .sel(OP), .in_0(c_0), .in_1(c_1), .in_2(1'b1), .in_3(1'b1), .in_4(1'b1), .in_5(1'b1), .in_6(1'b1),
    .in_7(1'b1), .out(carry));
  Multiplexer #(.Selector_Bits(3)) multiplexer_3 (
    .sel(OP), .in_0(n_0), .in_1(n_1), .in_2(n_2), .in_3(n_3), .in_4(n_4), .in_5(1'b0), .in_6(R0[1]),
    .in_7(1'b1), .out(negative));
  Multiplexer #(.Selector_Bits(3)) multiplexer_4 (
    .sel(OP), .in_0(z_0), .in_1(z_1), .in_2(z_2), .in_3(z_3), .in_4(z_4), .in_5(z_5), .in_6(z_6),
    .in_7(1'b1), .out(zero));

  // Other names for the same wires on the sheet: result_5[15:1] = R0[14:0]; n_6 = R0[1]; result_6[14:0] = R0[15:1];
  //   result_0[0] = n_0; result_1[0] = n_1; result_2[0] = n_2; result_3[0] = n_3; result_4[0] = n_4

  // Notes on the sheet:
  //   SUMA
  //   RESTA
  //   AND
  //   OR
  //   NOT
  //   LEFT BIT SHIFT
  //   RIGHT BIT SHIFT
endmodule
