// Digital circuit PC.dig as structural Verilog
module PC (
  input  CE,
  input  [5:0] D,
  input  LOAD,
  output [5:0] out
);

  CounterPreset #(.Bits(6)) counterpreset_1 (
    .en(1'b1), .C(CE), .dir(1'b0), .in(D), .ld(LOAD), .clr(1'b0), .out(out));  // open: ovf
endmodule
