// Digital circuit Unidad de ejecucion.dig as structural Verilog
module Unidad_de_ejecucion (
  input  EN_R0,
  input  EN_R1,
  input  LOAD_PC,
  input  STORE,
  input  ADRESS_PC____ADRESS_INSTRUCCION,
  input  CE_PC,
  input  [15:0] DATA,
  input  CLK,
  output Z,
  output N,
  output C,
  output [15:0] DATA_SALIDA,
  output [5:0] ADRESS
);

  wire alu_1_carry, alu_1_negative, alu_1_zero;
  wire [5:0] pc_1_out;
  wire [15:0] alu_1_result, datos_q, R0_q, R1_q;

  assign DATA_SALIDA = STORE ? datos_q : 16'bz;  // Driver driver_1
  Register u_Z (.D(alu_1_zero), .C(CLK), .en(1'b1), .Q(Z));
  Register #(.Bits(16)) datos (.D(alu_1_result), .C(CLK), .en(1'b1), .Q(datos_q));
  Register u_N (.D(alu_1_negative), .C(CLK), .en(1'b1), .Q(N));
  Register #(.Bits(16)) R1 (.D(DATA), .C(CLK), .en(EN_R1), .Q(R1_q));
  Register u_C (.D(alu_1_carry), .C(CLK), .en(1'b1), .Q(C));
  Register #(.Bits(16)) R0 (.D(DATA), .C(CLK), .en(EN_R0), .Q(R0_q));
  ALU alu_1 (
    .R0(R0_q), .R1(R1_q), .OP({DATA[13], DATA[14], DATA[15]}), .result(alu_1_result), .carry(alu_1_carry),
    .negative(alu_1_negative), .zero(alu_1_zero));
  Multiplexer #(.Bits(6)) multiplexer_1 (
    .sel(ADRESS_PC____ADRESS_INSTRUCCION), .in_0(DATA[5:0]), .in_1(pc_1_out), .out(ADRESS));
  PC pc_1 (.CE(CE_PC), .D(DATA[5:0]), .LOAD(LOAD_PC), .out(pc_1_out));

  // Other names for the same wires on the sheet: ADRESS_INSTRUCCION[5:0] = DATA[5:0];
  //   OP[2:0] = {DATA[13], DATA[14], DATA[15]}
endmodule
