// Digital circuit Decod6entradasconEnable.dig as structural Verilog
module Decod6entradasconEnable (
  input  [5:0] Adress,
  input  ENABLE,
  output Out_0,
  output Out_1,
  output Out_2,
  output Out_3,
  output Out_4,
  output Out_5,
  output Out_6,
  output Out_7,
  output Out_8,
  output Out_9,
  output Out_10,
  output Out_11,
  output Out_12,
  output Out_13,
  output Out_14,
  output Out_15,
  output Out_16,
  output Out_17,
  output Out_18,
  output Out_19,
  output Out_20,
  output Out_21,
  output Out_22,
  output Out_23,
  output Out_24,
  output Out_25,
  output Out_26,
  output Out_27,
  output Out_28,
  output Out_29,
  output Out_30,
  output Out_31,
  output Out_32,
  output Out_33,
  output Out_34,
  output Out_35,
  output Out_36,
  output Out_37,
  output Out_38,
  output Out_39,
  output Out_40,
  output Out_41,
  output Out_42,
  output Out_43,
  output Out_44,
  output Out_45,
  output Out_46,
  output Out_47,
  output Out_48,
  output Out_49,
  output Out_50,
  output Out_51,
  output Out_52,
  output Out_53,
  output Out_54,
  output Out_55,
  output Out_56,
  output Out_57,
  output Out_58,
  output Out_59,
  output Out_60,
  output Out_61,
  output Out_62,
  output Out_63
);

  wire decoder_1_out_0, decoder_1_out_1, decoder_1_out_2, decoder_1_out_3, decoder_1_out_4, decoder_1_out_5,
       decoder_1_out_6, decoder_1_out_7, decoder_1_out_8, decoder_1_out_9, decoder_1_out_10,
       decoder_1_out_11, decoder_1_out_12, decoder_1_out_13, decoder_1_out_14, decoder_1_out_15,
       decoder_1_out_16, decoder_1_out_17, decoder_1_out_18, decoder_1_out_19, decoder_1_out_20,
       decoder_1_out_21, decoder_1_out_22, decoder_1_out_23, decoder_1_out_24, decoder_1_out_25,
       decoder_1_out_27, decoder_1_out_28, decoder_1_out_29, decoder_1_out_30, decoder_1_out_31,
       decoder_1_out_32, decoder_1_out_33, decoder_1_out_34, decoder_1_out_35, decoder_1_out_36,
       decoder_1_out_37, decoder_1_out_38, decoder_1_out_39, decoder_1_out_40, decoder_1_out_41,
       decoder_1_out_42, decoder_1_out_43, decoder_1_out_44, decoder_1_out_45, decoder_1_out_46,
       decoder_1_out_47, decoder_1_out_48, decoder_1_out_49, decoder_1_out_50, decoder_1_out_51,
       decoder_1_out_52, decoder_1_out_53, decoder_1_out_54, decoder_1_out_55, decoder_1_out_56,
       decoder_1_out_57, decoder_1_out_58, decoder_1_out_59, decoder_1_out_60, decoder_1_out_61,
       decoder_1_out_62, decoder_1_out_63;

  Decoder #(.Selector_Bits(6)) decoder_1 (
    .sel(Adress), .out_0(decoder_1_out_0), .out_1(decoder_1_out_1), .out_2(decoder_1_out_2),
    .out_3(decoder_1_out_3), .out_4(decoder_1_out_4), .out_5(decoder_1_out_5), .out_6(decoder_1_out_6),
    .out_7(decoder_1_out_7), .out_8(decoder_1_out_8), .out_9(decoder_1_out_9), .out_10(decoder_1_out_10),
    .out_11(decoder_1_out_11), .out_12(decoder_1_out_12), .out_13(decoder_1_out_13),
    .out_14(decoder_1_out_14), .out_15(decoder_1_out_15), .out_16(decoder_1_out_16),
    .out_17(decoder_1_out_17), .out_18(decoder_1_out_18), .out_19(decoder_1_out_19),
    .out_20(decoder_1_out_20), .out_21(decoder_1_out_21), .out_22(decoder_1_out_22),
    .out_23(decoder_1_out_23), .out_24(decoder_1_out_24), .out_25(decoder_1_out_25),
    .out_26(decoder_1_out_25), .out_27(decoder_1_out_27), .out_28(decoder_1_out_28),
    .out_29(decoder_1_out_29), .out_30(decoder_1_out_30), .out_31(decoder_1_out_31),
    .out_32(decoder_1_out_32), .out_33(decoder_1_out_33), .out_34(decoder_1_out_34),
    .out_35(decoder_1_out_35), .out_36(decoder_1_out_36), .out_37(decoder_1_out_37),
    .out_38(decoder_1_out_38), .out_39(decoder_1_out_39), .out_40(decoder_1_out_40),
    .out_41(decoder_1_out_41), .out_42(decoder_1_out_42), .out_43(decoder_1_out_43),
    .out_44(decoder_1_out_44), .out_45(decoder_1_out_45), .out_46(decoder_1_out_46),
    .out_47(decoder_1_out_47), .out_48(decoder_1_out_48), .out_49(decoder_1_out_49),
    .out_50(decoder_1_out_50), .out_51(decoder_1_out_51), .out_52(decoder_1_out_52),
    .out_53(decoder_1_out_53), .out_54(decoder_1_out_54), .out_55(decoder_1_out_55),
    .out_56(decoder_1_out_56), .out_57(decoder_1_out_57), .out_58(decoder_1_out_58),
    .out_59(decoder_1_out_59), .out_60(decoder_1_out_60), .out_61(decoder_1_out_61),
    .out_62(decoder_1_out_62), .out_63(decoder_1_out_63));
  assign Out_0 = ENABLE ? decoder_1_out_0 : 1'bz;  // Driver driver_1
  assign Out_1 = ENABLE ? decoder_1_out_1 : 1'bz;  // Driver driver_2
  assign Out_2 = ENABLE ? decoder_1_out_2 : 1'bz;  // Driver driver_3
  assign Out_3 = ENABLE ? decoder_1_out_3 : 1'bz;  // Driver driver_4
  assign Out_4 = ENABLE ? decoder_1_out_4 : 1'bz;  // Driver driver_5
  assign Out_5 = ENABLE ? decoder_1_out_5 : 1'bz;  // Driver driver_6
  assign Out_6 = ENABLE ? decoder_1_out_6 : 1'bz;  // Driver driver_7
  assign Out_7 = ENABLE ? decoder_1_out_7 : 1'bz;  // Driver driver_8
  assign Out_8 = ENABLE ? decoder_1_out_8 : 1'bz;  // Driver driver_9
  assign Out_9 = ENABLE ? decoder_1_out_9 : 1'bz;  // Driver driver_10
  assign Out_10 = ENABLE ? decoder_1_out_10 : 1'bz;  // Driver driver_11
  assign Out_11 = ENABLE ? decoder_1_out_11 : 1'bz;  // Driver driver_12
  assign Out_12 = ENABLE ? decoder_1_out_12 : 1'bz;  // Driver driver_13
  assign Out_13 = ENABLE ? decoder_1_out_13 : 1'bz;  // Driver driver_14
  assign Out_14 = ENABLE ? decoder_1_out_14 : 1'bz;  // Driver driver_15
  assign Out_15 = ENABLE ? decoder_1_out_15 : 1'bz;  // Driver driver_16
  assign Out_16 = ENABLE ? decoder_1_out_16 : 1'bz;  // Driver driver_17
  assign Out_17 = ENABLE ? decoder_1_out_17 : 1'bz;  // Driver driver_18
  assign Out_18 = ENABLE ? decoder_1_out_18 : 1'bz;  // Driver driver_19
  assign Out_19 = ENABLE ? decoder_1_out_19 : 1'bz;  // Driver driver_20
  assign Out_20 = ENABLE ? decoder_1_out_20 : 1'bz;  // Driver driver_21
  assign Out_21 = ENABLE ? decoder_1_out_21 : 1'bz;  // Driver driver_22
  assign Out_22 = ENABLE ? decoder_1_out_22 : 1'bz;  // Driver driver_23
  assign Out_23 = ENABLE ? decoder_1_out_23 : 1'bz;  // Driver driver_24
  assign Out_24 = ENABLE ? decoder_1_out_24 : 1'bz;  // Driver driver_25
  assign Out_25 = ENABLE ? decoder_1_out_25 : 1'bz;  // Driver driver_26
  assign Out_26 = ENABLE ? decoder_1_out_25 : 1'bz;  // Driver driver_27
  assign Out_27 = ENABLE ? decoder_1_out_27 : 1'bz;  // Driver driver_28
  assign Out_28 = ENABLE ? decoder_1_out_28 : 1'bz;  // Driver driver_29
  assign Out_29 = ENABLE ? decoder_1_out_29 : 1'bz;  // Driver driver_30
  assign Out_30 = ENABLE ? decoder_1_out_30 : 1'bz;  // Driver driver_31
  assign Out_31 = ENABLE ? decoder_1_out_31 : 1'bz;  // Driver driver_32
  assign Out_32 = ENABLE ? decoder_1_out_32 : 1'bz;  // Driver driver_33
  assign Out_33 = ENABLE ? decoder_1_out_33 : 1'bz;  // Driver driver_34
  assign Out_34 = ENABLE ? decoder_1_out_34 : 1'bz;  // Driver driver_35
  assign Out_35 = ENABLE ? decoder_1_out_35 : 1'bz;  // Driver driver_36
  assign Out_36 = ENABLE ? decoder_1_out_36 : 1'bz;  // Driver driver_37
  assign Out_37 = ENABLE ? decoder_1_out_37 : 1'bz;  // Driver driver_38
  assign Out_38 = ENABLE ? decoder_1_out_38 : 1'bz;  // Driver driver_39
  assign Out_39 = ENABLE ? decoder_1_out_39 : 1'bz;  // Driver driver_40
  assign Out_40 = ENABLE ? decoder_1_out_40 : 1'bz;  // Driver driver_41
  assign Out_41 = ENABLE ? decoder_1_out_41 : 1'bz;  // Driver driver_42
  assign Out_42 = ENABLE ? decoder_1_out_42 : 1'bz;  // Driver driver_43
  assign Out_43 = ENABLE ? decoder_1_out_43 : 1'bz;  // Driver driver_44
  assign Out_44 = ENABLE ? decoder_1_out_44 : 1'bz;  // Driver driver_45
  assign Out_45 = ENABLE ? decoder_1_out_45 : 1'bz;  // Driver driver_46
  assign Out_46 = ENABLE ? decoder_1_out_46 : 1'bz;  // Driver driver_47
  assign Out_47 = ENABLE ? decoder_1_out_47 : 1'bz;  // Driver driver_48
  assign Out_48 = ENABLE ? decoder_1_out_48 : 1'bz;  // Driver driver_49
  assign Out_49 = ENABLE ? decoder_1_out_49 : 1'bz;  // Driver driver_50
  assign Out_50 = ENABLE ? decoder_1_out_50 : 1'bz;  // Driver driver_51
  assign Out_51 = ENABLE ? decoder_1_out_51 : 1'bz;  // Driver driver_52
  assign Out_52 = ENABLE ? decoder_1_out_52 : 1'bz;  // Driver driver_53
  assign Out_53 = ENABLE ? decoder_1_out_53 : 1'bz;  // Driver driver_54
  assign Out_54 = ENABLE ? decoder_1_out_54 : 1'bz;  // Driver driver_55
  assign Out_55 = ENABLE ? decoder_1_out_55 : 1'bz;  // Driver driver_56
  assign Out_56 = ENABLE ? decoder_1_out_56 : 1'bz;  // Driver driver_57
  assign Out_57 = ENABLE ? decoder_1_out_57 : 1'bz;  // Driver driver_58
  assign Out_58 = ENABLE ? decoder_1_out_58 : 1'bz;  // Driver driver_59
  assign Out_59 = ENABLE ? decoder_1_out_59 : 1'bz;  // Driver driver_60
  assign Out_60 = ENABLE ? decoder_1_out_60 : 1'bz;  // Driver driver_61
  assign Out_61 = ENABLE ? decoder_1_out_61 : 1'bz;  // Driver driver_62
  assign Out_62 = ENABLE ? decoder_1_out_62 : 1'bz;  // Driver driver_63
  assign Out_63 = ENABLE ? decoder_1_out_63 : 1'bz;  // Driver driver_64

  // Other names for the same wires on the sheet: EN = ENABLE
endmodule
