// Digital circuit Flip Flop pro.dig as structural Verilog
module Flip_Flop_pro (
  input  D,
  input  CLK,
  input  EN,
  output Q,
  output Q_2
);

  wire and_1_out;

  and and_1 (and_1_out, CLK, EN);
  D_FF d_ff_1 (.D(D), .C(and_1_out), .Q(Q), .nQ(Q_2));

  // Notes on the sheet:
  //   EN: ENABLE
endmodule
