// Digital circuit Memoria principal.dig as structural Verilog
module Memoria_principal (
  input  [15:0] Data_in,
  input  CLK,
  input  EN,
  input  [5:0] Adress,
  input  R_W,
  output [15:0] Data_out
);

  wire and_1_out, and_2_out, EN_0, EN_1, EN_2, EN_3, EN_4, EN_5, EN_6, EN_7, EN_8, EN_9, EN_10, EN_11, EN_12,
       EN_13, EN_14, EN_15, EN_16, EN_17, EN_18, EN_19, EN_20, EN_21, EN_22, EN_23, EN_24, EN_25, EN_26,
       EN_27, EN_28, EN_29, EN_30, EN_31, EN_32, EN_33, EN_34, EN_35, EN_36, EN_37, EN_38, EN_39, EN_40,
       EN_41, EN_42, EN_43, EN_44, EN_45, EN_46, EN_47, EN_48, EN_49, EN_50, EN_51, EN_52, EN_53, EN_54,
       EN_55, EN_56, EN_57, EN_58, EN_59, EN_60, EN_61, EN_62, EN_63, not_1_out;
  wire [15:0] Out_5, Out_6, Out_7, Out_8, Out_9, Out_10, Out_11, Out_12, Out_13, Out_14, Out_15, Out_16,
       Out_17, Out_18, Out_19, Out_20, Out_21, Out_22, Out_23, Out_24, Out_25, Out_26, Out_27, Out_28,
       Out_29, Out_30, Out_31, Out_32, Out_33, Out_34, Out_35, Out_36, Out_37, Out_38, Out_39, Out_40,
       Out_41, Out_42, Out_43, Out_44, Out_45, Out_46, Out_47, Out_48, Out_49, Out_50, Out_51, Out_52,
       Out_53, Out_54, Out_55, Out_56, Out_57, Out_58, Out_59, Out_60, Out_61, Out_62, Out_63,
       palabra_de_memoria_17_out;

  not not_1 (not_1_out, R_W);
  and and_1 (and_1_out, EN, not_1_out);
  Decod6entradasconEnable decod6entradasconenable_1 (
    .Adress(Adress), .ENABLE(and_1_out), .Out_0(EN_0), .Out_1(EN_1), .Out_2(EN_2), .Out_3(EN_3),
    .Out_4(EN_4), .Out_5(EN_5), .Out_6(EN_6), .Out_7(EN_7), .Out_8(EN_8), .Out_9(EN_9), .Out_10(EN_10),
    .Out_11(EN_11), .Out_12(EN_12), .Out_13(EN_13), .Out_14(EN_14), .Out_15(EN_15), .Out_16(EN_16),
    .Out_17(EN_17), .Out_18(EN_18), .Out_19(EN_19), .Out_20(EN_20), .Out_21(EN_21), .Out_22(EN_22),
    .Out_23(EN_23), .Out_24(EN_24), .Out_25(EN_25), .Out_26(EN_26), .Out_27(EN_27), .Out_28(EN_28),
    .Out_29(EN_29), .Out_30(EN_30), .Out_31(EN_31), .Out_32(EN_32), .Out_33(EN_33), .Out_34(EN_34),
    .Out_35(EN_35), .Out_36(EN_36), .Out_37(EN_37), .Out_38(EN_38), .Out_39(EN_39), .Out_40(EN_40),
    .Out_41(EN_41), .Out_42(EN_42), .Out_43(EN_43), .Out_44(EN_44), .Out_45(EN_45), .Out_46(EN_46),
    .Out_47(EN_47), .Out_48(EN_48), .Out_49(EN_49), .Out_50(EN_50), .Out_51(EN_51), .Out_52(EN_52),
    .Out_53(EN_53), .Out_54(EN_54), .Out_55(EN_55), .Out_56(EN_56), .Out_57(EN_57), .Out_58(EN_58),
    .Out_59(EN_59), .Out_60(EN_60), .Out_61(EN_61), .Out_62(EN_62), .Out_63(EN_63));
  Palabra_de_memoria palabra_de_memoria_1 (.EN(EN_0), .CLK(CLK), .D(Data_in));  // open: Out
  Palabra_de_memoria palabra_de_memoria_2 (.EN(EN_8), .CLK(CLK), .D(Data_in), .Out(Out_8));
  Palabra_de_memoria palabra_de_memoria_3 (.EN(EN_16), .CLK(CLK), .D(Data_in), .Out(Out_16));
  Palabra_de_memoria palabra_de_memoria_4 (.EN(EN_24), .CLK(CLK), .D(Data_in), .Out(Out_24));
  Palabra_de_memoria palabra_de_memoria_5 (.EN(EN_32), .CLK(CLK), .D(Data_in), .Out(Out_32));
  Palabra_de_memoria palabra_de_memoria_6 (.EN(EN_40), .CLK(CLK), .D(Data_in), .Out(Out_40));
  Palabra_de_memoria palabra_de_memoria_7 (.EN(EN_48), .CLK(CLK), .D(Data_in), .Out(Out_48));
  Palabra_de_memoria palabra_de_memoria_8 (.EN(EN_56), .CLK(CLK), .D(Data_in), .Out(Out_56));
  Palabra_de_memoria palabra_de_memoria_9 (.EN(EN_1), .CLK(CLK), .D(Data_in));  // open: Out
  Palabra_de_memoria palabra_de_memoria_10 (.EN(EN_9), .CLK(CLK), .D(Data_in), .Out(Out_9));
  Palabra_de_memoria palabra_de_memoria_11 (.EN(EN_17), .CLK(CLK), .D(Data_in), .Out(Out_17));
  Palabra_de_memoria palabra_de_memoria_12 (.EN(EN_25), .CLK(CLK), .D(Data_in), .Out(Out_25));
  Palabra_de_memoria palabra_de_memoria_13 (.EN(EN_33), .CLK(CLK), .D(Data_in), .Out(Out_33));
  Palabra_de_memoria palabra_de_memoria_14 (.EN(EN_41), .CLK(CLK), .D(Data_in), .Out(Out_41));
  Palabra_de_memoria palabra_de_memoria_15 (.EN(EN_49), .CLK(CLK), .D(Data_in), .Out(Out_49));
  Palabra_de_memoria palabra_de_memoria_16 (.EN(EN_57), .CLK(CLK), .D(Data_in), .Out(Out_57));
  Palabra_de_memoria palabra_de_memoria_17 (.EN(EN_2), .CLK(CLK), .D(Data_in), .Out(palabra_de_memoria_17_out));
  Palabra_de_memoria palabra_de_memoria_18 (.EN(EN_10), .CLK(CLK), .D(Data_in), .Out(Out_10));
  Palabra_de_memoria palabra_de_memoria_19 (.EN(EN_18), .CLK(CLK), .D(Data_in), .Out(Out_18));
  Palabra_de_memoria palabra_de_memoria_20 (.EN(EN_26), .CLK(CLK), .D(Data_in), .Out(Out_26));
  Palabra_de_memoria palabra_de_memoria_21 (.EN(EN_34), .CLK(CLK), .D(Data_in), .Out(Out_34));
  Palabra_de_memoria palabra_de_memoria_22 (.EN(EN_42), .CLK(CLK), .D(Data_in), .Out(Out_42));
  Palabra_de_memoria palabra_de_memoria_23 (.EN(EN_50), .CLK(CLK), .D(Data_in), .Out(Out_50));
  Palabra_de_memoria palabra_de_memoria_24 (.EN(EN_58), .CLK(CLK), .D(Data_in), .Out(Out_58));
  Palabra_de_memoria palabra_de_memoria_25 (.EN(EN_3), .CLK(CLK), .D(Data_in));  // open: Out
  Palabra_de_memoria palabra_de_memoria_26 (.EN(EN_11), .CLK(CLK), .D(Data_in), .Out(Out_11));
  Palabra_de_memoria palabra_de_memoria_27 (.EN(EN_19), .CLK(CLK), .D(Data_in), .Out(Out_19));
  Palabra_de_memoria palabra_de_memoria_28 (.EN(EN_27), .CLK(CLK), .D(Data_in), .Out(Out_27));
  Palabra_de_memoria palabra_de_memoria_29 (.EN(EN_35), .CLK(CLK), .D(Data_in), .Out(Out_35));
  Palabra_de_memoria palabra_de_memoria_30 (.EN(EN_43), .CLK(CLK), .D(Data_in), .Out(Out_43));
  Palabra_de_memoria palabra_de_memoria_31 (.EN(EN_51), .CLK(CLK), .D(Data_in), .Out(Out_51));
  Palabra_de_memoria palabra_de_memoria_32 (.EN(EN_59), .CLK(CLK), .D(Data_in), .Out(Out_59));
  Palabra_de_memoria palabra_de_memoria_33 (.EN(EN_4), .CLK(CLK), .D(Data_in));  // open: Out
  Palabra_de_memoria palabra_de_memoria_34 (.EN(EN_12), .CLK(CLK), .D(Data_in), .Out(Out_12));
  Palabra_de_memoria palabra_de_memoria_35 (.EN(EN_20), .CLK(CLK), .D(Data_in), .Out(Out_20));
  Palabra_de_memoria palabra_de_memoria_36 (.EN(EN_28), .CLK(CLK), .D(Data_in), .Out(Out_28));
  Palabra_de_memoria palabra_de_memoria_37 (.EN(EN_36), .CLK(CLK), .D(Data_in), .Out(Out_36));
  Palabra_de_memoria palabra_de_memoria_38 (.EN(EN_44), .CLK(CLK), .D(Data_in), .Out(Out_44));
  Palabra_de_memoria palabra_de_memoria_39 (.EN(EN_52), .CLK(CLK), .D(Data_in), .Out(Out_52));
  Palabra_de_memoria palabra_de_memoria_40 (.EN(EN_60), .CLK(CLK), .D(Data_in), .Out(Out_60));
  Palabra_de_memoria palabra_de_memoria_41 (.EN(EN_5), .CLK(CLK), .D(Data_in), .Out(Out_5));
  Palabra_de_memoria palabra_de_memoria_42 (.EN(EN_13), .CLK(CLK), .D(Data_in), .Out(Out_13));
  Palabra_de_memoria palabra_de_memoria_43 (.EN(EN_21), .CLK(CLK), .D(Data_in), .Out(Out_21));
  Palabra_de_memoria palabra_de_memoria_44 (.EN(EN_29), .CLK(CLK), .D(Data_in), .Out(Out_29));
  Palabra_de_memoria palabra_de_memoria_45 (.EN(EN_37), .CLK(CLK), .D(Data_in), .Out(Out_37));
  Palabra_de_memoria palabra_de_memoria_46 (.EN(EN_45), .CLK(CLK), .D(Data_in), .Out(Out_45));
  Palabra_de_memoria palabra_de_memoria_47 (.EN(EN_53), .CLK(CLK), .D(Data_in), .Out(Out_53));
  Palabra_de_memoria palabra_de_memoria_48 (.EN(EN_61), .CLK(CLK), .D(Data_in), .Out(Out_61));
  Palabra_de_memoria palabra_de_memoria_49 (.EN(EN_6), .CLK(CLK), .D(Data_in), .Out(Out_6));
  Palabra_de_memoria palabra_de_memoria_50 (.EN(EN_14), .CLK(CLK), .D(Data_in), .Out(Out_14));
  Palabra_de_memoria palabra_de_memoria_51 (.EN(EN_22), .CLK(CLK), .D(Data_in), .Out(Out_22));
  Palabra_de_memoria palabra_de_memoria_52 (.EN(EN_30), .CLK(CLK), .D(Data_in), .Out(Out_30));
  Palabra_de_memoria palabra_de_memoria_53 (.EN(EN_38), .CLK(CLK), .D(Data_in), .Out(Out_38));
  Palabra_de_memoria palabra_de_memoria_54 (.EN(EN_46), .CLK(CLK), .D(Data_in), .Out(Out_46));
  Palabra_de_memoria palabra_de_memoria_55 (.EN(EN_54), .CLK(CLK), .D(Data_in), .Out(Out_54));
  Palabra_de_memoria palabra_de_memoria_56 (.EN(EN_62), .CLK(CLK), .D(Data_in), .Out(Out_62));
  Palabra_de_memoria palabra_de_memoria_57 (.EN(EN_7), .CLK(CLK), .D(Data_in), .Out(Out_7));
  Palabra_de_memoria palabra_de_memoria_58 (.EN(EN_15), .CLK(CLK), .D(Data_in), .Out(Out_15));
  Palabra_de_memoria palabra_de_memoria_59 (.EN(EN_23), .CLK(CLK), .D(Data_in), .Out(Out_23));
  Palabra_de_memoria palabra_de_memoria_60 (.EN(EN_31), .CLK(CLK), .D(Data_in), .Out(Out_31));
  Palabra_de_memoria palabra_de_memoria_61 (.EN(EN_39), .CLK(CLK), .D(Data_in), .Out(Out_39));
  Palabra_de_memoria palabra_de_memoria_62 (.EN(EN_47), .CLK(CLK), .D(Data_in), .Out(Out_47));
  Palabra_de_memoria palabra_de_memoria_63 (.EN(EN_55), .CLK(CLK), .D(Data_in), .Out(Out_55));
  Palabra_de_memoria palabra_de_memoria_64 (.EN(EN_63), .CLK(CLK), .D(Data_in), .Out(Out_63));
  and and_2 (and_2_out, EN, R_W);
  Mux6entradasconEnable mux6entradasconenable_1 (
    .Enable(and_2_out), .Adress(Adress), .In_0({16{1'b0}}), .In_1(16'h1), .In_2(16'h2), .In_3(16'h3),
    .In_4(16'h4), .In_5(Out_5), .In_6(Out_6), .In_7(Out_7), .In_8(Out_8), .In_9(Out_9), .In_10(Out_10),
    .In_11(Out_11), .In_12(Out_12), .In_13(Out_13), .In_14(Out_14), .In_15(Out_15), .In_16(Out_16),
    .In_17(Out_17), .In_18(Out_18), .In_19(Out_19), .In_20(Out_20), .In_21(Out_21), .In_22(Out_22),
    .In_23(Out_23), .In_24(Out_24), .In_25(Out_25), .In_26(Out_26), .In_27(Out_27), .In_28(Out_28),
    .In_29(Out_29), .In_30(Out_30), .In_31(Out_31), .In_32(Out_32), .In_33(Out_33), .In_34(Out_34),
    .In_35(Out_35), .In_36(Out_36), .In_37(Out_37), .In_38(Out_38), .In_39(Out_39), .In_40(Out_40),
    .In_41(Out_41), .In_42(Out_42), .In_43(Out_43), .In_44(Out_44), .In_45(Out_45), .In_46(Out_46),
    .In_47(Out_47), .In_48(Out_48), .In_49(Out_49), .In_50(Out_50), .In_51(Out_51), .In_52(Out_52),
    .In_53(Out_53), .In_54(Out_54), .In_55(Out_55), .In_56(Out_56), .In_57(Out_57), .In_58(Out_58),
    .In_59(Out_59), .In_60(Out_60), .In_61(Out_61), .In_62(Out_62), .In_63(Out_63), .Out(Data_out));

  // Other names for the same wires on the sheet: EN_GENERAL = EN
endmodule
