// Digital circuit Mux6entradasconEnable.dig as structural Verilog
module Mux6entradasconEnable (
  input  Enable,
  input  [5:0] Adress,
  input  [15:0] In_0,
  input  [15:0] In_1,
  input  [15:0] In_2,
  input  [15:0] In_3,
  input  [15:0] In_4,
  input  [15:0] In_5,
  input  [15:0] In_6,
  input  [15:0] In_7,
  input  [15:0] In_8,
  input  [15:0] In_9,
  input  [15:0] In_10,
  input  [15:0] In_11,
  input  [15:0] In_12,
  input  [15:0] In_13,
  input  [15:0] In_14,
  input  [15:0] In_15,
  input  [15:0] In_16,
  input  [15:0] In_17,
  input  [15:0] In_18,
  input  [15:0] In_19,
  input  [15:0] In_20,
  input  [15:0] In_21,
  input  [15:0] In_22,
  input  [15:0] In_23,
  input  [15:0] In_24,
  input  [15:0] In_25,
  input  [15:0] In_26,
  input  [15:0] In_27,
  input  [15:0] In_28,
  input  [15:0] In_29,
  input  [15:0] In_30,
  input  [15:0] In_31,
  input  [15:0] In_32,
  input  [15:0] In_33,
  input  [15:0] In_34,
  input  [15:0] In_35,
  input  [15:0] In_36,
  input  [15:0] In_37,
  input  [15:0] In_38,
  input  [15:0] In_39,
  input  [15:0] In_40,
  input  [15:0] In_41,
  input  [15:0] In_42,
  input  [15:0] In_43,
  input  [15:0] In_44,
  input  [15:0] In_45,
  input  [15:0] In_46,
  input  [15:0] In_47,
  input  [15:0] In_48,
  input  [15:0] In_49,
  input  [15:0] In_50,
  input  [15:0] In_51,
  input  [15:0] In_52,
  input  [15:0] In_53,
  input  [15:0] In_54,
  input  [15:0] In_55,
  input  [15:0] In_56,
  input  [15:0] In_57,
  input  [15:0] In_58,
  input  [15:0] In_59,
  input  [15:0] In_60,
  input  [15:0] In_61,
  input  [15:0] In_62,
  input  [15:0] In_63,
  output [15:0] Out
);

  wire [15:0] multiplexer_1_out;

  Multiplexer #(.Selector_Bits(6), .Bits(16)) multiplexer_1 (
    .sel(Adress), .in_0(In_0), .in_1(In_1), .in_2(In_2), .in_3(In_3), .in_4(In_4), .in_5(In_5), .in_6(In_6),
    .in_7(In_7), .in_8(In_8), .in_9(In_9), .in_10(In_10), .in_11(In_11), .in_12(In_12), .in_13(In_13),
    .in_14(In_14), .in_15(In_15), .in_16(In_16), .in_17(In_17), .in_18(In_18), .in_19(In_19), .in_20(In_20),
    .in_21(In_21), .in_22(In_22), .in_23(In_23), .in_24(In_24), .in_25(In_25), .in_26(In_26), .in_27(In_27),
    .in_28(In_28), .in_29(In_29), .in_30(In_30), .in_31(In_31), .in_32(In_32), .in_33(In_33), .in_34(In_34),
    .in_35(In_35), .in_36(In_36), .in_37(In_37), .in_38(In_38), .in_39(In_39), .in_40(In_40), .in_41(In_41),
    .in_42(In_42), .in_43(In_43), .in_44(In_44), .in_45(In_45), .in_46(In_46), .in_47(In_47), .in_48(In_48),
    .in_49(In_49), .in_50(In_50), .in_51(In_51), .in_52(In_52), .in_53(In_53), .in_54(In_54), .in_55(In_55),
    .in_56(In_56), .in_57(In_57), .in_58(In_58), .in_59(In_59), .in_60(In_60), .in_61(In_61), .in_62(In_62),
    .in_63(In_63), .out(multiplexer_1_out));
  assign Out = Enable ? multiplexer_1_out : 16'bz;  // Driver driver_1
endmodule
