// Digital circuit Palabra de memoria.dig as structural Verilog
module Palabra_de_memoria (
  input  EN,
  input  CLK,
  input  [15:0] D,
  output [15:0] Out
);

  Flip_Flop_pro flip_flop_pro_1 (.D(D[0]), .CLK(CLK), .EN(EN), .Q(Out[0]));  // open: Q_2
  Flip_Flop_pro flip_flop_pro_2 (.D(D[1]), .CLK(CLK), .EN(EN), .Q(Out[1]));  // open: Q_2
  Flip_Flop_pro flip_flop_pro_3 (.D(D[2]), .CLK(CLK), .EN(EN), .Q(Out[2]));  // open: Q_2
  Flip_Flop_pro flip_flop_pro_4 (.D(D[3]), .CLK(CLK), .EN(EN), .Q(Out[3]));  // open: Q_2
  Flip_Flop_pro flip_flop_pro_5 (.D(D[4]), .CLK(CLK), .EN(EN), .Q(Out[4]));  // open: Q_2
  Flip_Flop_pro flip_flop_pro_6 (.D(D[5]), .CLK(CLK), .EN(EN), .Q(Out[5]));  // open: Q_2
  Flip_Flop_pro flip_flop_pro_7 (.D(D[6]), .CLK(CLK), .EN(EN), .Q(Out[6]));  // open: Q_2
  Flip_Flop_pro flip_flop_pro_8 (.D(D[7]), .CLK(CLK), .EN(EN), .Q(Out[7]));  // open: Q_2
  Flip_Flop_pro flip_flop_pro_9 (.D(D[8]), .CLK(CLK), .EN(EN), .Q(Out[8]));  // open: Q_2
  Flip_Flop_pro flip_flop_pro_10 (.D(D[9]), .CLK(CLK), .EN(EN), .Q(Out[9]));  // open: Q_2
  Flip_Flop_pro flip_flop_pro_11 (.D(D[10]), .CLK(CLK), .EN(EN), .Q(Out[10]));  // open: Q_2
  Flip_Flop_pro flip_flop_pro_12 (.D(D[11]), .CLK(CLK), .EN(EN), .Q(Out[11]));  // open: Q_2
  Flip_Flop_pro flip_flop_pro_13 (.D(D[12]), .CLK(CLK), .EN(EN), .Q(Out[12]));  // open: Q_2
  Flip_Flop_pro flip_flop_pro_14 (.D(D[13]), .CLK(CLK), .EN(EN), .Q(Out[13]));  // open: Q_2
  Flip_Flop_pro flip_flop_pro_15 (.D(D[14]), .CLK(CLK), .EN(EN), .Q(Out[14]));  // open: Q_2
  Flip_Flop_pro flip_flop_pro_16 (.D(D[15]), .CLK(CLK), .EN(EN), .Q(Out[15]));  // open: Q_2

  // Other names for the same wires on the sheet: D_0 = D[0]; D_1 = D[1]; D_2 = D[2]; D_3 = D[3]; D_4 = D[4];
  //   D_5 = D[5]; D_6 = D[6]; D_7 = D[7]; D_8 = D[8]; D_9 = D[9]; D_10 = D[10]; D_11 = D[11]; D_12 = D[12];
  //   D_13 = D[13]; D_14 = D[14]; D_15 = D[15]; Out_0 = Out[0]; Out_1 = Out[1]; Out_2 = Out[2]; Out_3 = Out[3];
  //   Out_4 = Out[4]; Out_5 = Out[5]; Out_6 = Out[6]; Out_7 = Out[7]; Out_8 = Out[8]; Out_9 = Out[9];
  //   Out_10 = Out[10]; Out_11 = Out[11]; Out_12 = Out[12]; Out_13 = Out[13]; Out_14 = Out[14]; Out_15 = Out[15]
endmodule
