// Digital circuit arbitro.dig as structural Verilog
module arbitro (
  input  BR_CPU,
  input  BR_MEMORIA,
  output BG_CPU,
  output BG_MEMORIA
);

  PriorityEncoder priorityencoder_1 (.in0(BR_MEMORIA), .in1(BR_CPU), .num(BG_CPU));  // open: any
  not not_1 (BG_MEMORIA, BG_CPU);

  // Notes on the sheet:
  //   Si num vale 0, se ha concedido 
  //   bus grant a memoria
  //   si num vale 1, se ha concedido 
  //   bus grant a cpu
endmodule
