// Digital circuit contador sin reset automatico.dig as structural Verilog
module contador_sin_reset_automatico (
  input  CLK,
  output Z1,
  output Z0
);

  wire d_ff_2_nq, or_1_out, or_2_out;

  D_FF d_ff_1 (.D(or_1_out), .C(CLK), .Q(Z1));  // open: nQ
  D_FF d_ff_2 (.D(or_2_out), .C(CLK), .Q(Z0), .nQ(d_ff_2_nq));
  or or_1 (or_1_out, Z1, Z0);
  or or_2 (or_2_out, Z1, d_ff_2_nq);
endmodule
