// Digital circuit main.dig as structural Verilog
module main (
  input  clk,
  input  ON,
  input  [15:0] cargar_data,
  input  [5:0] cargar_adress,
  input  cargar_me,
  input  cargar_rw
);

  wire and_1_out, contador_sin_reset_automatico_1_z0, contador_sin_reset_automatico_1_z1, cpu_1_me,
       cpu_1_r_w, driver_1_out, driver_4_out, driver_5_out, multiplexer_1_out, not_1_out;
  wire [5:0] cpu_1_adress, driver_3_out;
  wire [15:0] cpu_1_data_out, driver_2_out, memoria_principal_1_out;

  Multiplexer multiplexer_1 (.sel(ON), .in_0(1'b0), .in_1(clk), .out(multiplexer_1_out));
  contador_sin_reset_automatico contador_sin_reset_automatico_1 (
    .CLK(multiplexer_1_out), .Z1(contador_sin_reset_automatico_1_z1), .Z0(contador_sin_reset_automatico_1_z0));
  and and_1 (and_1_out, not_1_out, contador_sin_reset_automatico_1_z0);
  not not_1 (not_1_out, contador_sin_reset_automatico_1_z1);
  assign driver_1_out = and_1_out ? and_1_out : 1'bz;  // Driver driver_1
  CPU cpu_1 (
    .DATA_in(memoria_principal_1_out), .CLK(clk), .START(driver_1_out), .Data_out(cpu_1_data_out),
    .Adress(cpu_1_adress), .ME(cpu_1_me), .R_W(cpu_1_r_w));
  assign driver_2_out = ON ? cpu_1_data_out : 16'bz;  // Driver driver_2
  assign driver_3_out = ON ? cpu_1_adress : 6'bz;  // Driver driver_3
  assign driver_4_out = ON ? cpu_1_me : 1'bz;  // Driver driver_4
  assign driver_5_out = ON ? cpu_1_r_w : 1'bz;  // Driver driver_5
  assign driver_2_out = ~ON ? cargar_data : 16'bz;  // DriverInvSel driverinvsel_1
  assign driver_3_out = ~ON ? cargar_adress : 6'bz;  // DriverInvSel driverinvsel_2
  assign driver_4_out = ~ON ? cargar_me : 1'bz;  // DriverInvSel driverinvsel_3
  LedMatrix #(.colAddrBits(1), .rowDataBits(16)) ledmatrix_1 (.rows(memoria_principal_1_out), .column(1'b1));
  assign driver_5_out = ~ON ? cargar_rw : 1'bz;  // DriverInvSel driverinvsel_4
  Memoria_principal memoria_principal_1 (
    .CLK(clk), .Data(driver_2_out), .Adress(driver_3_out), .EN(driver_4_out), .R_W(driver_5_out),
    .out(memoria_principal_1_out));

  // Notes on the sheet:
  //   clk: Hz: 3
  //   Si estamos en el primer ciclo, 
  //   se envia el pulso de start.
  //   Si estamos en cualquier otro
  //   ciclo no se hace nada
  //   (se envia alta impedancia)
endmodule
